# Fritzing sketch CoronaMultitool (saved by Fritzing 0.9.3b)
breadboards: 3

parts:
  Part1 = BME280 Breakout
  MH-Z1 = MH-Z14 [part_number=MH-Z14]
  DHT1 = DHT22 Humidity and Temperature Sensor
  Part2 = Arduino Nano (Rev3.0)
  Grove1 = Grove OLED 128x96
  Part3 = KY-012 Active Buzzer Module [package="Breakout board"]
  LED1 = smd LED [color="Red (633nm)" package="0603 [SMD]"]
  HC-SR04_Sensor_1 = HC-SR04 Ultrasonic Distance Sensor
  R2 = Resistor [tolerance=±5% resistance=220 package=THT]
  MH-Z2 = MH-Z14 [part_number=MH-Z14]
  LLC1 = Logic Level Converter [package="Breakout board"]  # not connected
  Part4 = Arduino Nano (Rev3.0)
  MH-Z3 = MH-Z14 [part_number=MH-Z14]
  Part5 = Arduino Nano (Rev3.0)

nets:
  GND: Part1.GND, DHT1.GND, Part2.GND, Grove1.GND, Part3.-, LED1.cathode, HC-SR04_Sensor_1.GND
  3.3V: Part1.3.3V, MH-Z1.5, DHT1.VDD, Part2.5V, HC-SR04_Sensor_1.VCC
  N1: Part1.SDI/SDA, Part2.A4, Grove1.SDA
  N2: Part1.SCK/SCL, Part2.A5, Grove1.SCL
  N3: MH-Z1.12, Part2.D3
  N4: DHT1.DATA, Part2.D2
  N5: Part2.D5, HC-SR04_Sensor_1.TRIG
  N6: Part2.D6, HC-SR04_Sensor_1.ECHO
  N7: Part2.D7, R2.Pin_0
  N8: Part2.D8, Part3.S
  3V3: Part2.3V3, Grove1.VCC
  N9: LED1.anode, R2.Pin_1
  N10: MH-Z2.5, Part4.5V
  N11: MH-Z3.5, Part5.5V
  N12: MH-Z3.7, Part5.GND

notes:
  PWM: 17:5V, 16:GND, 6:D3
  --> CO2 value: too high
  UART: A0, A1
  Serial:

custom parts:
  MH-Z14: MH-Z14 NDIR Infrared gas module is a common type, small size sensor, using non-dispersive infrared (NDIR) principle to detect the existence of CO2 in the air, with good selectivity, non-oxygen dependant, long life. Built-in temperature sensor can do temperature compensation; and it has digital output and analog voltage output.
  KY-012 Active Buzzer Module: Active Piezoelectric Buzzer Module Keyes KY-012, it produces single-tone sound when signal is high.
  Logic Level Converter: 5V to/from 3.3V logic level converter
